// Logisim project ALU.circ as structural Verilog: 4 circuits, main circuit main
module main (
  input  [15:0] A,
  input  [15:0] B,
  input  [15:0] imm,
  input  [4:0] shamt,
  input  [5:0] Opcode,
  output [15:0] out_6
);

  wire comparator_1_lt;
  wire [15:0] and_1_out, multiplexer_1_out, multiplier_1_out, n16_bit_adder_1_sum, n16_bit_adder_2_sum,
       or_1_out, shifter_1_out, subtractor_1_out;

  _16_Bit_Adder u_16_bit_adder_1 (.A(A), .B(B), .Sum(n16_bit_adder_1_sum));  // open: Cout
  Subtractor #(.width(16)) subtractor_1 (.a(A), .b(B), .out(subtractor_1_out));  // open: bin, bout
  Multiplier #(.width(16)) multiplier_1 (.a(A), .b(B), .out(multiplier_1_out));  // open: cin, cout
  assign and_1_out = A & B;  // AND_Gate and_1, 16 bits wide
  assign or_1_out = A | B;  // OR_Gate or_1, 16 bits wide
  _16_Bit_Adder u_16_bit_adder_2 (.A(A), .B(imm), .Sum(n16_bit_adder_2_sum));  // open: Cout
  Shifter #(.width(16)) shifter_1 (.in(A), .\dist (shamt[3:0]), .out(shifter_1_out));
  Comparator #(.width(16)) comparator_1 (.a(A), .b(B), .lt(comparator_1_lt));  // open: gt, eq
  Multiplexer #(.width(16)) multiplexer_1 (
    .in0({16{1'b0}}), .in1(16'h1), .out(multiplexer_1_out), .sel(comparator_1_lt), .en(1'b1));
  Multiplexer #(.select(4), .width(16)) multiplexer_2 (
    .in0(n16_bit_adder_1_sum), .in1(subtractor_1_out), .in2(multiplier_1_out), .in3(and_1_out),
    .in4(or_1_out), .in5(n16_bit_adder_2_sum), .in6(shifter_1_out), .in7(multiplexer_1_out), .out(out_6),
    .sel(Opcode[3:0]));  // open: in8, in9, in10, in11, in12, in13, in14, in15, en
endmodule

module _1_bit_Adder (
  input  Cin,
  input  A,
  input  B,
  output Sum,
  output Cout
);

  wire and_1_out, and_2_out, xor_1_out;

  xor xor_1 (xor_1_out, Cin, A);
  xor xor_2 (Sum, xor_1_out, B);
  and and_1 (and_1_out, A, Cin);
  and and_2 (and_2_out, xor_1_out, B);
  or or_1 (Cout, and_1_out, and_2_out);
endmodule

module _4_bit_Adder (
  input  Cin,
  input  [3:0] A,
  input  [3:0] B,
  output [3:0] Sum,
  output Cout
);

  wire n1_bit_adder_1_cout, n1_bit_adder_2_cout, n1_bit_adder_3_cout;

  _1_bit_Adder u_1_bit_adder_1 (.Cin(Cin), .A(A[0]), .B(B[0]), .Sum(Sum[0]), .Cout(n1_bit_adder_1_cout));
  _1_bit_Adder u_1_bit_adder_2 (
    .Cin(n1_bit_adder_1_cout), .A(A[1]), .B(B[1]), .Sum(Sum[1]), .Cout(n1_bit_adder_2_cout));
  _1_bit_Adder u_1_bit_adder_3 (
    .Cin(n1_bit_adder_2_cout), .A(A[2]), .B(B[2]), .Sum(Sum[2]), .Cout(n1_bit_adder_3_cout));
  _1_bit_Adder u_1_bit_adder_4 (.Cin(n1_bit_adder_3_cout), .A(A[3]), .B(B[3]), .Sum(Sum[3]), .Cout(Cout));
endmodule

// Adder
module _16_Bit_Adder (
  input  [15:0] A,
  input  [15:0] B,
  output [15:0] Sum,
  output Cout
);

  wire n4_bit_adder_1_cout, n4_bit_adder_2_cout, n4_bit_adder_3_cout;

  _4_bit_Adder u_4_bit_adder_1 (.Cin(1'b0), .A(A[3:0]), .B(B[3:0]), .Sum(Sum[3:0]), .Cout(n4_bit_adder_1_cout));
  _4_bit_Adder u_4_bit_adder_2 (
    .Cin(n4_bit_adder_1_cout), .A(A[7:4]), .B(B[7:4]), .Sum(Sum[7:4]), .Cout(n4_bit_adder_2_cout));
  _4_bit_Adder u_4_bit_adder_3 (
    .Cin(n4_bit_adder_2_cout), .A(A[11:8]), .B(B[11:8]), .Sum(Sum[11:8]), .Cout(n4_bit_adder_3_cout));
  _4_bit_Adder u_4_bit_adder_4 (.Cin(n4_bit_adder_3_cout), .A(A[15:12]), .B(B[15:12]), .Sum(Sum[15:12]), .Cout(Cout));
endmodule
